# Fritzing sketch Diagrama (saved by Fritzing 0.9.0b)
breadboards: 1

parts:
  Part1 = Arduino Uno (Rev3)
  S1 = Pushbutton [package="[THT]"]
  S2 = Pushbutton [package="[THT]"]
  R2 = Rotary Potentiometer (Large) [maximum_resistance=5kΩ package=THT]
  R3 = Rotary Potentiometer (Large) [maximum_resistance=5kΩ package=THT]
  R4 = Resistor [tolerance=±5% resistance=10k package=THT]
  R5 = Resistor [tolerance=±5% resistance=10k package=THT]

nets:
  N1: Part1.A0, R2.wiper
  N2: Part1.A1, R3.wiper
  N3: Part1.D8, S2.Pin_3, S2.Pin_4, R4.Pin_1
  N4: Part1.D7, S1.Pin_1, S1.Pin_2, R5.Pin_0
  N5: Part1.5V, R2.leg2, R3.leg2, R4.Pin_0, R5.Pin_1
  N6: Part1.GND, S1.Pin_3, S1.Pin_4, S2.Pin_1, S2.Pin_2, R2.leg1, R3.leg1

notes:
  VCC GND SCL SDA
  Del display OLED
